# Fritzing sketch Schematic Tx (saved by Fritzing 0.9.3b)
breadboards: 1

parts:
  Atmega1 = ATmega328 [package=tqfp]
  Part1 = Tri-Axis Gyro Breakout - L3G4200D
  Part2 = Tri-Axis Gyro Breakout - L3G4200D
  Part3 = NRF24L01+ Breakout Board

nets:
  GND: Atmega1.GND, Part1.GND, Part2.GND, Part3.GND
  N1: Atmega1.PB1(OC1A), Part3.CE
  N2: Atmega1.PB2(SS_OC1B), Part3.CS
  N3: Atmega1.PB3(MOSI_OC2), Part3.MOSI
  N4: Atmega1.PB4(MISO), Part3.MISO
  N5: Atmega1.PB5(SCK), Part3.SCK
  VCC: Atmega1.AVCC, Part1.SDO, Part2.VCC, Part3.VCC
  N6: Atmega1.PC4(ADC4_SDA), Part1.SDA, Part2.SDA
  N7: Atmega1.PC5(ADC5_SCL), Part1.SCL, Part2.SCL
  N8: Atmega1.PD2(INT0), Part3.IRQ
